// Logisim project 10_template_Sequential.circ as structural Verilog: 9 circuits, main circuit Task1
module Eg1 (
  input  Set,
  input  Set_2,
  input  Reset,
  input  Reset_2,
  input  Inputs,
  input  Inputs_2,
  input  S,
  input  R,
  input  Start,
  input  set_all_to_0,
  output Q,
  output Not_Q,
  output Not_Q_2,
  output Q_2,
  output Outputs,
  output out_16,
  output out_17,
  output out_18,
  output out_19,
  output out_20,
  output Q_3,
  output NOT_Q_3
);

  wire clock_1_out, clock_2_out, Clock_3_out, clock_4_out, clock_5_out, d_ff_2_q;

  Clock clock_1 (.out(clock_1_out));
  Clock clock_2 (.out(clock_2_out));
  Clock Clock_3 (.out(Clock_3_out));
  D_Flip_Flop d_ff_1 (.clk(clock_2_out), .D(out_17), .Q(out_17), .Qn(out_19));  // open: preset, en, reset
  Clock clock_4 (.out(clock_4_out));
  D_Flip_Flop d_ff_2 (.clk(Clock_3_out), .D(Start), .Q(d_ff_2_q), .reset(set_all_to_0));  // open: Qn, preset, en
  nand nand_1 (Q, Set, Not_Q_2);
  nand nand_2 (Not_Q_2, Q, Reset);
  D_Flip_Flop d_ff_3 (.clk(clock_1_out), .D(Inputs), .Q(Outputs), .Qn(out_16));  // open: preset, en, reset
  D_Flip_Flop d_ff_4 (.clk(Clock_3_out), .D(d_ff_2_q), .reset(set_all_to_0));  // open: Q, Qn, preset, en
  Clock clock_5 (.out(clock_5_out));
  D_Flip_Flop d_ff_5 (.clk(clock_4_out), .D(Inputs_2), .Q(Q_3), .Qn(NOT_Q_3), .preset(S), .reset(R));  // open: en
  D_Flip_Flop d_ff_6 (.clk(clock_5_out), .D(out_20), .Q(out_18), .Qn(out_20));  // open: preset, en, reset
  nor nor_1 (Not_Q, Set_2, Q_2);
  nor nor_2 (Q_2, Not_Q, Reset_2);

  // Notes on the sheet:
  //   ---------------------------------------------------------------------------------------------------------------------------------------
  //   Study 'D Flip-Flop' (D,clock,Q and *Q*) from 'Memory'  tree section on the left.
  //   Clock:  Simulate/tick frequency/0.5Hz
  //   When Clock goes from 0 to 1 the 'D Flip=flop' sets outputs Q=D and *Q*=Not(D) 
  //   ---------------------------------------------------------------------------------------------------------------------------------------
  //   Study 'D Flip-Flop' circuits: D=Q or D=*Q* 
  //   ---------------------------------------------------------------------------------------------------------------------------------------
  //   Study 'D Flip-Flop' (S 'set' and R 'reset') inputs
  //   When S is set to 1, it sets Q to 1 and Q to 0. S is below R in the hierarchy.
  //   When R is set to 1, it sets Q to 0 and *Q* to 1. R is above S in the hierarchy.
  //   ---------------------------------------------------------------------------------------------------------------------------------------
  //   Study 'D Flip-Flop' register
  //   SR Flip-Flop NAND actives by low state (1->0)
  //   D=Q
  //   Valid states: S=1,R=0 -> Q=1,NotQ=0  OR  S=0,R=1 -> Q=0,NotQ=1
  //   S=0,R=0 -> invalid condition. S=1,R=1 depends on the past
  //   Q=D when S=R=0
  //   *Q*=Not(D) when S=R=0
  //   D=*Q*
  //   Outputs:
  //   SR Flip-Flop NOR actives by high state (0->1)
endmodule

module Task1 (
  input  Start,
  input  set_all_to_0
);

  wire Clock_out, d_ff_1_q;

  Clock Clock (.out(Clock_out));
  D_Flip_Flop d_ff_1 (.clk(Clock_out), .D(Start), .Q(d_ff_1_q), .reset(set_all_to_0));  // open: Qn, preset, en
  D_Flip_Flop d_ff_2 (.clk(Clock_out), .D(d_ff_1_q), .reset(set_all_to_0));  // open: Q, Qn, preset, en
  D_Flip_Flop d_ff_3 (.clk(Clock_out), .reset(set_all_to_0));  // open: D, Q, Qn, preset, en
  D_Flip_Flop d_ff_4 (.clk(Clock_out), .reset(set_all_to_0));  // open: D, Q, Qn, preset, en

  // Notes on the sheet:
  //   Task 1 Using D-type flip-flops build 4-bit shift register: 0000,1000,1100,1110,1111.
endmodule

module Task2 (
  input  set_all_to_0
);

  wire Clock_out, d_ff_1_q, d_ff_2_q, d_ff_3_q, d_ff_4_q;

  Clock Clock (.out(Clock_out));
  D_Flip_Flop d_ff_1 (.clk(Clock_out), .D(d_ff_4_q), .Q(d_ff_1_q), .reset(set_all_to_0));  // open: Qn, preset, en
  D_Flip_Flop d_ff_2 (.clk(Clock_out), .D(d_ff_1_q), .Q(d_ff_2_q), .reset(set_all_to_0));  // open: Qn, preset, en
  D_Flip_Flop d_ff_3 (.clk(Clock_out), .D(d_ff_2_q), .Q(d_ff_3_q), .reset(set_all_to_0));  // open: Qn, preset, en
  D_Flip_Flop d_ff_4 (.clk(Clock_out), .D(d_ff_3_q), .Q(d_ff_4_q), .reset(set_all_to_0));  // open: Qn, preset, en

  // Notes on the sheet:
  //   Task 2 Using shift register from point 1. build ring counter:
  //    the bits circulate through the connected stages in a circular fashion.
endmodule

module Task3 (
  input  set_all_to_0,
  output [3:0] out_2
);

  wire Clock_out, d_ff_4_qn;

  Clock Clock (.out(Clock_out));
  D_Flip_Flop d_ff_1 (.clk(Clock_out), .D(d_ff_4_qn), .Q(out_2[0]), .reset(set_all_to_0));  // open: Qn, preset, en
  D_Flip_Flop d_ff_2 (.clk(Clock_out), .D(out_2[0]), .Q(out_2[1]), .reset(set_all_to_0));  // open: Qn, preset, en
  D_Flip_Flop d_ff_3 (.clk(Clock_out), .D(out_2[1]), .Q(out_2[2]), .reset(set_all_to_0));  // open: Qn, preset, en
  D_Flip_Flop d_ff_4 (
    .clk(Clock_out), .D(out_2[2]), .Q(out_2[3]), .Qn(d_ff_4_qn), .reset(set_all_to_0));  // open: preset, en

  // Notes on the sheet:
  //   Task 3 Using shift register from point 1. build Johnson counter:
  //   0000,0001,0011,0111,1111,1110,1100,1000,0000
endmodule

module Eg2 (
  input  set_all_to_0,
  output [3:0] out_2
);

  wire Clock_out, d_ff_1_qn, d_ff_2_qn, d_ff_3_qn, d_ff_4_qn;

  Clock Clock (.out(Clock_out));
  Hex_Digit_Display hex_digit_display_1 (.value(out_2));  // open: dp
  D_Flip_Flop d_ff_1 (
    .clk(Clock_out), .D(d_ff_1_qn), .Q(out_2[0]), .Qn(d_ff_1_qn), .reset(set_all_to_0));  // open: preset, en
  D_Flip_Flop d_ff_2 (
    .clk(d_ff_1_qn), .D(d_ff_2_qn), .Q(out_2[1]), .Qn(d_ff_2_qn), .reset(set_all_to_0));  // open: preset, en
  D_Flip_Flop d_ff_3 (
    .clk(d_ff_2_qn), .D(d_ff_3_qn), .Q(out_2[2]), .Qn(d_ff_3_qn), .reset(set_all_to_0));  // open: preset, en
  D_Flip_Flop d_ff_4 (
    .clk(d_ff_3_qn), .D(d_ff_4_qn), .Q(out_2[3]), .Qn(d_ff_4_qn), .reset(set_all_to_0));  // open: preset, en

  // Notes on the sheet:
  //   D-type flip-flops 4-bit counter from 0 to 15
endmodule

module Task4 (
  input  set_0001,
  output [3:0] out_2
);

  wire Clock_out, xor_1_out;

  Clock Clock (.out(Clock_out));
  Hex_Digit_Display hex_digit_display_1 (.value(out_2));  // open: dp
  D_Flip_Flop d_ff_1 (.clk(Clock_out), .D(xor_1_out), .Q(out_2[0]), .preset(set_0001));  // open: Qn, en, reset
  D_Flip_Flop d_ff_2 (.clk(Clock_out), .D(out_2[0]), .Q(out_2[1]), .reset(set_0001));  // open: Qn, preset, en
  D_Flip_Flop d_ff_3 (.clk(Clock_out), .D(out_2[1]), .Q(out_2[2]), .reset(set_0001));  // open: Qn, preset, en
  D_Flip_Flop d_ff_4 (.clk(Clock_out), .D(out_2[2]), .Q(out_2[3]), .reset(set_0001));  // open: Qn, preset, en
  xor xor_1 (xor_1_out, out_2[2], out_2[3]);

  // Notes on the sheet:
  //   Task 4 Using shift register from point 1. and XOR logic gate make PRBS
  //   Pseudo Random Binary Signal generator
endmodule

module Eg3 (
  input  set_all_to_0,
  output [3:0] out_2
);

  wire Clock_out, d_ff_1_qn, d_ff_2_qn, d_ff_3_qn, d_ff_4_qn;

  Clock Clock (.out(Clock_out));
  Hex_Digit_Display hex_digit_display_1 (.value(out_2));  // open: dp
  D_Flip_Flop d_ff_1 (
    .clk(Clock_out), .D(d_ff_1_qn), .Q(out_2[0]), .Qn(d_ff_1_qn), .reset(set_all_to_0));  // open: preset, en
  D_Flip_Flop d_ff_2 (
    .clk(d_ff_1_qn), .D(d_ff_2_qn), .Q(out_2[1]), .Qn(d_ff_2_qn), .preset(set_all_to_0));  // open: en, reset
  D_Flip_Flop d_ff_3 (
    .clk(d_ff_2_qn), .D(d_ff_3_qn), .Q(out_2[2]), .Qn(d_ff_3_qn), .preset(set_all_to_0));  // open: en, reset
  D_Flip_Flop d_ff_4 (
    .clk(d_ff_3_qn), .D(d_ff_4_qn), .Q(out_2[3]), .Qn(d_ff_4_qn), .reset(set_all_to_0));  // open: preset, en

  // Notes on the sheet:
  //   D-type flip-flops 4-bit set a start number 0110
endmodule

module Task5 (
  output [3:0] out_1
);

  wire and_1_out, Clock_out, d_ff_4_qn;

  Clock Clock (.out(Clock_out));
  Hex_Digit_Display hex_digit_display_1 (.value(out_1));  // open: dp
  D_Flip_Flop d_ff_1 (.clk(Clock_out), .D(d_ff_4_qn), .Q(out_1[0]), .reset(and_1_out));  // open: Qn, preset, en
  D_Flip_Flop d_ff_2 (.Q(out_1[1]), .reset(and_1_out));  // open: clk, D, Qn, preset, en
  D_Flip_Flop d_ff_3 (.Q(out_1[2]), .reset(and_1_out));  // open: clk, D, Qn, preset, en
  D_Flip_Flop d_ff_4 (.Q(out_1[3]), .Qn(d_ff_4_qn), .reset(and_1_out));  // open: clk, D, preset, en
  and and_1 (and_1_out, out_1[3], out_1[0]);

  // Notes on the sheet:
  //   Task 5 Using D-type flip-flops build mod9 counter (from 0000 to 1000 )
  //   Set all to 0
endmodule

module Task6 (
  output [3:0] out_1
);

  wire and_1_out, Clock_out, d_ff_1_qn, d_ff_2_qn, d_ff_3_qn, d_ff_4_qn;

  Clock Clock (.out(Clock_out));
  Hex_Digit_Display hex_digit_display_1 (.value(out_1));  // open: dp
  D_Flip_Flop d_ff_1 (
    .clk(Clock_out), .D(d_ff_1_qn), .Q(out_1[0]), .Qn(d_ff_1_qn), .preset(and_1_out));  // open: en, reset
  D_Flip_Flop d_ff_2 (
    .clk(d_ff_1_qn), .D(d_ff_2_qn), .Q(out_1[1]), .Qn(d_ff_2_qn), .preset(and_1_out));  // open: en, reset
  D_Flip_Flop d_ff_3 (
    .clk(d_ff_2_qn), .D(d_ff_3_qn), .Q(out_1[2]), .Qn(d_ff_3_qn), .reset(and_1_out));  // open: preset, en
  D_Flip_Flop d_ff_4 (
    .clk(d_ff_3_qn), .D(d_ff_4_qn), .Q(out_1[3]), .Qn(d_ff_4_qn), .reset(and_1_out));  // open: preset, en
  and and_1 (and_1_out, out_1[3], out_1[0]);

  // Notes on the sheet:
  //   Task 6 Using D-type flip-flops build counter from X to Y
  //   The values of X and Y in task 6 are assigned according to your place in the classroom. 
  //   Set start
endmodule
