// Logisim project 07 and 08 lab mobile robot.circ as structural Verilog: 6 circuits, main circuit 04 LM
module _04_LM (
  input  a,
  input  b,
  input  c,
  output LM
);

  wire a__b_out, a__c_out, minus_b__c_out, not_1_out, not_2_out;

  not not_1 (not_1_out, b);
  not not_2 (not_2_out, c);
  and a__c (a__c_out, a, not_2_out);
  or OR (LM, a__c_out, a__b_out, minus_b__c_out);
  and a__b (a__b_out, a, not_1_out);
  and minus_b__c (minus_b__c_out, not_1_out, not_2_out);

  // Notes on the sheet:
  //   4. Using Logisim, create LM logic circuits and check it.
endmodule

module _04_RM (
  input  a,
  input  b,
  input  c,
  output RM
);

  wire minus_b_c_out, not_1_out, not_2_out;

  not not_1 (not_1_out, a);
  not not_2 (not_2_out, b);
  and minus_b_c (minus_b_c_out, not_2_out, c);
  nor minus_a___b_c (RM, not_1_out, minus_b_c_out);

  // Notes on the sheet:
  //   4. Using Logisim, create RM logic circuits and check it.
  //   (not a) or (not b and c)
endmodule

module _05_RM_NAND_only (
  input  a,
  input  b,
  input  c,
  input  a_2,
  input  b_2,
  input  c_2,
  input  NOT,
  input  in_8,
  input  AND,
  input  in_10,
  input  in_11,
  input  in_12,
  input  OR,
  input  in_14,
  input  in_15,
  input  in_16,
  output RM,
  output RM_2,
  output out_19,
  output out_20,
  output out_21,
  output out_22,
  output out_23,
  output out_24
);

  wire minus_b_c_out, nand_1_out, nand_2_out, nand_3_out, nand_4_out, nand_6_out, nand_7_out, nand_8_out,
       nand_9_out, nand_10_out, not_1_out, not_2_out;

  not not_1 (not_1_out, a);
  not not_2 (not_2_out, b);
  and minus_b_c (minus_b_c_out, not_2_out, c);
  nand nand_1 (nand_1_out, a_2, a_2);
  nand nand_2 (nand_2_out, b_2, b_2);
  not not_3 (out_19, NOT);
  and and_1 (out_21, AND, in_11);
  or or_1 (out_23, OR, in_15);
  or minus_a___b_c (RM, not_1_out, minus_b_c_out);
  nand nand_3 (nand_3_out, nand_2_out, c_2);
  nand nand_4 (nand_4_out, nand_3_out, nand_3_out);
  nand nand_5 (out_20, in_8, in_8);
  nand nand_6 (nand_6_out, in_10, in_12);
  nand nand_7 (nand_7_out, in_14, in_14);
  nand nand_8 (nand_8_out, in_16, in_16);
  nand nand_9 (nand_9_out, nand_1_out, nand_1_out);
  nand nand_10 (nand_10_out, nand_4_out, nand_4_out);
  nand nand_11 (out_22, nand_6_out, nand_6_out);
  nand nand_12 (out_24, nand_7_out, nand_8_out);
  nand nand_13 (RM_2, nand_9_out, nand_10_out);

  // Notes on the sheet:
  //   Substitution rules
  //   5. Create RM logic circuits. Replace OR, AND, NOT by NAND and check it.
endmodule

module _07_LM__NOT_and_NAND_only (
  input  a,
  input  b,
  input  c,
  output out_4
);

  wire nand_1_out, nand_2_out, nand_3_out, not_1_out, not_2_out;

  not not_1 (not_1_out, b);
  not not_2 (not_2_out, c);
  nand nand_1 (nand_1_out, a, not_2_out);
  nand nand_2 (nand_2_out, a, not_1_out);
  nand nand_3 (nand_3_out, not_1_out, not_2_out);
  nand nand_4 (out_4, nand_1_out, nand_2_out, nand_3_out);

  // Notes on the sheet:
  //   7. Using Logisim, create LM logic circuit
  //   Use NAND, NOT gates and check it.
endmodule

module _07_RM__NOT_and_NAND_only (
  input  a,
  input  b,
  input  c,
  output out_4
);

  wire nand_1_out, not_1_out;

  not not_1 (not_1_out, b);
  nand nand_1 (nand_1_out, not_1_out, c);
  nand nand_2 (out_4, a, nand_1_out);

  // Notes on the sheet:
  //   7. Using Logisim, create RM logic circuit
  //   Use NAND, NOT gates and check it.
  //   a Nand (not b Nand c)  
endmodule

module _1_E (
  input  a,
  input  b,
  input  c,
  output OUT
);

  wire nand_1_out, nand_2_out, nand_3_out, not_1_out, not_2_out;

  not not_1 (not_1_out, a);
  not not_2 (not_2_out, b);
  nand nand_1 (nand_1_out, not_1_out, not_2_out);
  nand nand_2 (nand_2_out, not_1_out, c);
  nand nand_3 (nand_3_out, not_2_out, c);
  nand nand_4 (OUT, nand_1_out, nand_2_out, nand_3_out);
endmodule
